// Digital circuit LIMP_VERSION3.dig as structural Verilog
module LIMP_VERSION3 (
  input  in1,
  input  in2,
  input  in3,
  input  in4,
  input  in_5,
  input  in_6,
  input  in_7,
  input  in_8,
  input  in_9,
  input  in_10
);

  wire _74139_1_p9, _74139_1_p10, _74139_1_p11, _74139_1_p12, _74139_1_p13, _74139_1_p14, _74139_1_p15,
       _74139_1_p16, _74154_1_p9, _74154_1_p10, _74154_1_p11, _74154_1_p12, _74154_1_p13, _74154_1_p14,
       _74154_1_p15, _74154_1_p16, _74154_1_p17, _74154_1_p18, _74175_1_p9, _74175_1_p10, _74175_1_p11,
       _74175_1_p12, _74175_5_p9, _74175_5_p10, _74175_5_p11, _74175_5_p12, _74191_1_p1, _74191_1_p2,
       _74191_1_p3, _74191_1_p4, _74191_1_p5, _74191_1_p10, _74191_1_p11, _74191_1_p12, _74191_1_p13,
       _74191_1_p14, _74191_1_p15, _74191_2_p1, _74191_2_p2, _74191_2_p3, _74191_2_p4, _74191_2_p10,
       _74191_2_p11, _74191_2_p12, _74191_2_p13, _74191_2_p14, _74191_2_p15, _74191_3_p1, _74191_3_p2,
       _74191_3_p3, _74191_3_p4, _74191_3_p10, _74191_3_p11, _74191_3_p12, _74191_3_p13, _74191_3_p14,
       _74244_1_p13, _74244_1_p14, _74244_1_p15, _74244_1_p16, _74244_2_p6, _74244_2_p7, _74244_2_p8,
       _74244_2_p9, _74244_2_p13, _74244_2_p14, _74244_2_p15, _74244_2_p16, _74244_3_p17, _74244_3_p18,
       _74244_3_p19, _74244_3_p20, _74244_4_p11, _74244_4_p12, _74244_4_p13, _74244_4_p14, _74244_4_p15,
       _74244_4_p16, _74244_5_p13, _74244_5_p14, _74244_5_p15, _74244_5_p16, _744017_1_p3, _744017_1_p6,
       _744017_1_p7, _744017_1_p8, _744017_1_p9, _744017_1_p10, _744017_1_p11, and_3_out, and_4_out,
       and_5_out, and_6_out, and_7_out, and_8_out, and_9_out, and_10_out, and_11_out, and_12_out, and_13_out,
       button_1_out, d_ff_1_q, d_ff_2_q, delay_1_out, driver_1_out, driver_4_out, driverinvsel_1_out,
       driverinvsel_2_out, driverinvsel_5_out, driverinvsel_7_out, driverinvsel_11_out, driverinvsel_14_out,
       driverinvsel_15_out, driverinvsel_16_out, nor_1_out, nor_2_out, not_1_out, not_2_out, not_3_out,
       not_4_out, not_5_out, not_6_out, not_7_out, not_8_out, not_9_out, not_10_out, not_11_out, not_12_out,
       not_13_out, not_14_out, not_15_out, or_1_out, or_2_out, or_3_out, or_4_out, pulldown_11_out,
       pullup_4_out, xnor_1_out, xnor_2_out, xnor_3_out, xnor_4_out, xor_1_out, xor_2_out, xor_3_out,
       xor_4_out, xor_5_out, xor_6_out, xor_7_out, xor_8_out;
  wire [3:0] _74244_1_p1, _74244_2_p4, _74373_1_p13, _74373_2_p13, _74373_3_p13;

  assign driverinvsel_1_out = ~_74154_1_p11 ? _74154_1_p11 : 1'bz;  // DriverInvSel driverinvsel_1
  assign driverinvsel_2_out = ~pullup_4_out ? pullup_4_out : 1'bz;  // DriverInvSel driverinvsel_2
  assign driverinvsel_2_out = ~_74154_1_p11 ? _74154_1_p11 : 1'bz;  // DriverInvSel driverinvsel_3
  PullUp pullup_1 (.out(driverinvsel_1_out));
  Button button_1 (.out(button_1_out));
  PullUp pullup_2 (.out(driverinvsel_2_out));
  // _74191 _74191_1: pin names not known; wires that end beside it: _74191_1_p1, _74191_1_p2, _74191_1_p3, _74191_1_p4, _74191_1_p5, 1'b0, driverinvsel_2_out, 1'b0, 1'b0, _74191_1_p10, _74191_1_p11, _74191_1_p12, _74191_1_p13, _74191_1_p14, _74191_1_p15
  PullUp pullup_3 (.out(_74191_1_p5));
  // _74191 _74191_2: pin names not known; wires that end beside it: _74191_2_p1, _74191_2_p2, _74191_2_p3, _74191_2_p4, _74191_1_p5, 1'b0, driverinvsel_1_out, 1'b0, 1'b0, _74191_2_p10, _74191_2_p11, _74191_2_p12, _74191_2_p13, _74191_2_p14, _74191_2_p15
  // _74191 _74191_3: pin names not known; wires that end beside it: _74191_3_p1, _74191_3_p2, _74191_3_p3, _74191_3_p4, _74191_1_p5, 1'b0, driverinvsel_1_out, 1'b0, 1'b0, _74191_3_p10, _74191_3_p11, _74191_3_p12, _74191_3_p13, _74191_3_p14, _74191_3_p11, _74191_3_p12, _74191_3_p13, _74191_3_p14
  assign _74191_1_p10 = ~driver_1_out ? button_1_out : 1'bz;  // DriverInvSel driverinvsel_4
  assign driver_1_out = _744017_1_p3 ? _744017_1_p3 : 1'bz;  // Driver driver_1
  assign driver_1_out = _744017_1_p11 ? _744017_1_p11 : 1'bz;  // Driver driver_2
  PullDown pulldown_1 (.out(driver_1_out));
  PullDown pulldown_2 (.out(_74191_1_p10));
  nor nor_1 (nor_1_out, _74191_1_p12, _74191_1_p13, _74191_1_p14, _74191_1_p15);
  D_FF d_ff_1 (.D(_74191_2_p11), .C(button_1_out), .Q(d_ff_1_q));  // open: nQ
  nor nor_2 (nor_2_out, _74191_2_p12, _74191_2_p13, _74191_2_p14, _74191_2_p15);
  // _744017 _744017_1: pin names not known; wires that end beside it: 1'b0, button_1_out, _744017_1_p3, 1'b1, 1'b0, _744017_1_p6, _744017_1_p7, _744017_1_p8, _744017_1_p9, _744017_1_p10, _744017_1_p11, _744017_1_p3
  D_FF d_ff_2 (.D(_74191_1_p11), .C(button_1_out), .Q(d_ff_2_q));  // open: nQ
  and and_1 (_74191_2_p10, nor_1_out, d_ff_2_q);
  and and_2 (_74191_3_p10, d_ff_1_q, nor_2_out);
  assign driver_1_out = _744017_1_p6 ? _744017_1_p6 : 1'bz;  // Driver driver_3
  // _74175 _74175_1: pin names not known; wires that end beside it: _744017_1_p7, 1'b1, in1, in2, in3, in4, 1'b1, 1'b0, _74175_1_p9, _74175_1_p10, _74175_1_p11, _74175_1_p12
  // _74175 _74175_2: pin names not known; wires that end beside it: _744017_1_p8, 1'b1, in1, in2, in3, in4, 1'b1, 1'b0, _74191_1_p1, _74191_1_p2, _74191_1_p3, _74191_1_p4
  // _74175 _74175_3: pin names not known; wires that end beside it: _744017_1_p9, 1'b1, in1, in2, in3, in4, 1'b1, 1'b0, _74191_2_p1, _74191_2_p2, _74191_2_p3, _74191_2_p4
  // _74175 _74175_4: pin names not known; wires that end beside it: _744017_1_p10, 1'b1, in1, in2, in3, in4, 1'b1, 1'b0, _74191_3_p1, _74191_3_p2, _74191_3_p3, _74191_3_p4
  not not_1 (not_1_out, _744017_1_p11);
  // _74154 _74154_1: pin names not known; wires that end beside it: _74175_1_p9, _74175_1_p11, _74175_1_p10, _74175_1_p12, not_1_out, not_1_out, 1'b1, 1'b0, _74154_1_p9, _74154_1_p10, _74154_1_p11, _74154_1_p12, _74154_1_p13, _74154_1_p14, _74154_1_p15, _74154_1_p16, _74154_1_p17, _74154_1_p18
  // _74244 _74244_1: pin names not known; wires that end beside it: _74244_1_p1[3], _74244_1_p1[2], _74244_1_p1[1], _74244_1_p1[0], _74154_1_p13, _74191_3_p1, _74191_3_p2, _74191_3_p3, _74191_3_p4, _74154_1_p12, 1'b1, 1'b0, _74244_1_p13, _74244_1_p14, _74244_1_p15, _74244_1_p16, _74244_1_p13, _74244_1_p14, _74244_1_p15, _74244_1_p16
  assign driverinvsel_5_out = ~_74154_1_p10 ? _74154_1_p10 : 1'bz;  // DriverInvSel driverinvsel_5
  assign driverinvsel_5_out = ~_74154_1_p13 ? _74154_1_p13 : 1'bz;  // DriverInvSel driverinvsel_6
  assign driverinvsel_7_out = ~_74154_1_p15 ? _74154_1_p15 : 1'bz;  // DriverInvSel driverinvsel_7
  assign driverinvsel_7_out = ~_74154_1_p15 ? _74154_1_p15 : 1'bz;  // DriverInvSel driverinvsel_8
  assign driverinvsel_7_out = ~_74154_1_p14 ? _74154_1_p14 : 1'bz;  // DriverInvSel driverinvsel_9
  PullDown pulldown_3 (.out(_74244_1_p16));
  PullDown pulldown_4 (.out(_74244_1_p15));
  PullUp pullup_4 (.out(pullup_4_out));
  PullDown pulldown_5 (.out(_74244_1_p14));
  PullDown pulldown_6 (.out(_74244_1_p13));
  assign driverinvsel_5_out = ~_74154_1_p14 ? _74154_1_p14 : 1'bz;  // DriverInvSel driverinvsel_10
  assign driverinvsel_11_out = ~_74154_1_p14 ? _74154_1_p14 : 1'bz;  // DriverInvSel driverinvsel_11
  PullUp pullup_5 (.out(driverinvsel_7_out));
  PullUp pullup_6 (.out(driverinvsel_5_out));
  assign driverinvsel_5_out = ~_74154_1_p12 ? _74154_1_p12 : 1'bz;  // DriverInvSel driverinvsel_12
  assign driverinvsel_7_out = ~_74154_1_p14 ? _74154_1_p14 : 1'bz;  // DriverInvSel driverinvsel_13
  assign driverinvsel_14_out = ~_74154_1_p12 ? _74154_1_p12 : 1'bz;  // DriverInvSel driverinvsel_14
  not not_2 (not_2_out, driverinvsel_15_out);
  assign driverinvsel_15_out = ~_74154_1_p17 ? _74154_1_p17 : 1'bz;  // DriverInvSel driverinvsel_15
  assign driverinvsel_16_out = ~_74154_1_p17 ? _74154_1_p17 : 1'bz;  // DriverInvSel driverinvsel_16
  assign driverinvsel_16_out = ~_74154_1_p9 ? _74154_1_p9 : 1'bz;  // DriverInvSel driverinvsel_17
  not not_3 (not_3_out, _74154_1_p9);
  // _74244 _74244_2: pin names not known; wires that end beside it: _74244_2_p4[3], _74244_2_p4[2], _74244_2_p4[1], _74244_2_p4[0], not_2_out, _74244_2_p6, _74244_2_p7, _74244_2_p8, _74244_2_p9, _74154_1_p17, 1'b1, 1'b0, _74244_2_p13, _74244_2_p14, _74244_2_p15, _74244_2_p16, _74244_2_p13, _74244_2_p14, _74244_2_p15, _74244_2_p16
  assign driverinvsel_16_out = ~_74154_1_p10 ? _74154_1_p10 : 1'bz;  // DriverInvSel driverinvsel_18
  assign driverinvsel_11_out = ~_74154_1_p10 ? _74154_1_p10 : 1'bz;  // DriverInvSel driverinvsel_19
  // _74175 _74175_5: pin names not known; wires that end beside it: not_3_out, 1'b1, _74191_2_p1, _74191_2_p2, _74191_2_p3, _74191_2_p4, 1'b1, 1'b0, _74175_5_p9, _74175_5_p10, _74175_5_p11, _74175_5_p12
  PullUp pullup_7 (.out(driverinvsel_14_out));
  PullUp pullup_8 (.out(driverinvsel_16_out));
  assign driverinvsel_14_out = ~_74154_1_p13 ? _74154_1_p13 : 1'bz;  // DriverInvSel driverinvsel_20
  assign driverinvsel_11_out = ~_74154_1_p13 ? _74154_1_p13 : 1'bz;  // DriverInvSel driverinvsel_21
  // _74139 _74139_1: pin names not known; wires that end beside it: _74191_1_p1, _74191_1_p2, driverinvsel_16_out, _74191_2_p1, _74191_2_p2, driverinvsel_5_out, 1'b1, 1'b0, _74139_1_p9, _74139_1_p10, _74139_1_p11, _74139_1_p12, _74139_1_p13, _74139_1_p14, _74139_1_p15, _74139_1_p16
  PullUp pullup_9 (.out(driverinvsel_11_out));
  DiodeBackward #(.Blown("true")) diodebackward_1 (.in(driverinvsel_15_out), .out(driverinvsel_11_out));
  not not_4 (not_4_out, driverinvsel_11_out);
  // _74244 _74244_3: pin names not known; wires that end beside it: _74175_5_p9, _74175_5_p10, _74175_5_p11, _74175_5_p12, not_4_out, _74244_2_p4[3], _74244_2_p4[2], _74244_2_p4[1], _74244_2_p4[0], driverinvsel_14_out, 1'b1, 1'b0, _74244_2_p4[3], _74244_2_p4[2], _74244_2_p4[1], _74244_2_p4[0], _74244_3_p17, _74244_3_p18, _74244_3_p19, _74244_3_p20
  PullUp pullup_10 (.out(driverinvsel_15_out));
  PullDown pulldown_7 (.out(_74244_3_p20));
  PullDown pulldown_8 (.out(_74244_3_p19));
  not not_5 (not_5_out, _74139_1_p9);
  not not_6 (not_6_out, _74139_1_p10);
  not not_7 (not_7_out, _74139_1_p11);
  not not_8 (not_8_out, _74139_1_p12);
  PullDown pulldown_9 (.out(_74244_3_p18));
  PullDown pulldown_10 (.out(_74244_3_p17));
  Delay #(.delayTime(3)) delay_1 (.in(not_5_out), .out(delay_1_out));
  // _74175 _74175_6: pin names not known; wires that end beside it: delay_1_out, 1'b1, _74244_2_p13, _74244_2_p14, _74244_2_p15, _74244_2_p16, 1'b1, 1'b0, _74244_1_p1[3], _74244_1_p1[2], _74244_1_p1[1], _74244_1_p1[0]
  xnor xnor_1 (xnor_1_out, _74244_3_p17, _74244_1_p13);
  xnor xnor_2 (xnor_2_out, _74244_3_p18, _74244_1_p14);
  xnor xnor_3 (xnor_3_out, _74244_3_p19, _74244_1_p15);
  xnor xnor_4 (xnor_4_out, _74244_3_p20, _74244_1_p16);
  PowerSupply powersupply_1 (.VDD(in_9), .GND(in_10));
  assign pullup_4_out = ~driverinvsel_14_out ? not_9_out : 1'bz;  // DriverInvSel driverinvsel_22
  and and_3 (and_3_out, xnor_1_out, xnor_2_out);
  and and_4 (and_4_out, xnor_3_out, xnor_4_out);
  LED led_1 (.in(_74244_1_p1[3]));
  LED led_2 (.in(_74244_1_p1[2]));
  LED led_3 (.in(_74244_1_p1[1]));
  LED led_4 (.in(_74244_1_p1[0]));
  assign _74244_2_p4 = ~_74139_1_p13 ? _74244_1_p1 : 4'bz;  // DriverInvSel driverinvsel_23
  not not_9 (not_9_out, and_5_out);
  and and_5 (and_5_out, and_3_out, and_4_out);
  // _74373 _74373_1: pin names not known; wires that end beside it: 1'b0, not_6_out, _74244_2_p4[3], _74244_2_p4[2], _74244_2_p4[1], _74244_2_p4[0], 1'b1, 1'b1, 1'b1, 1'b1, 1'b1, 1'b0, _74373_1_p13[3], _74373_1_p13[2], _74373_1_p13[1], _74373_1_p13[0]
  LED led_5 (.in(_74373_1_p13[3]));
  LED led_6 (.in(_74373_1_p13[3]));
  LED led_7 (.in(_74373_1_p13[2]));
  LED led_8 (.in(_74373_1_p13[2]));
  LED led_9 (.in(_74373_1_p13[1]));
  LED led_10 (.in(_74373_1_p13[1]));
  LED led_11 (.in(_74373_1_p13[0]));
  LED led_12 (.in(_74373_1_p13[0]));
  assign _74244_2_p4 = ~_74139_1_p14 ? _74373_1_p13 : 4'bz;  // DriverInvSel driverinvsel_24
  xor xor_1 (xor_1_out, _74244_2_p6, _74244_2_p4[3]);
  and and_6 (and_6_out, _74244_2_p6, _74244_2_p4[3]);
  xor xor_2 (xor_2_out, _74244_2_p7, _74244_2_p4[2]);
  and and_7 (and_7_out, _74244_2_p7, _74244_2_p4[2]);
  xor xor_3 (xor_3_out, _74244_2_p8, _74244_2_p4[1]);
  and and_8 (and_8_out, _74244_2_p8, _74244_2_p4[1]);
  xor xor_4 (xor_4_out, _74244_2_p9, _74244_2_p4[0]);
  and and_9 (and_9_out, _74244_2_p9, _74244_2_p4[0]);
  xor xor_5 (xor_5_out, pulldown_11_out, xor_1_out);
  and and_10 (and_10_out, pulldown_11_out, xor_1_out);
  PullDown pulldown_11 (.out(pulldown_11_out));
  xor xor_6 (xor_6_out, or_1_out, xor_2_out);
  and and_11 (and_11_out, or_1_out, xor_2_out);
  xor xor_7 (xor_7_out, or_2_out, xor_3_out);
  and and_12 (and_12_out, or_2_out, xor_3_out);
  xor xor_8 (xor_8_out, or_3_out, xor_4_out);
  and and_13 (and_13_out, or_3_out, xor_4_out);
  or or_1 (or_1_out, and_10_out, and_6_out);
  or or_2 (or_2_out, and_11_out, and_7_out);
  or or_3 (or_3_out, and_12_out, and_8_out);
  or or_4 (or_4_out, and_13_out, and_9_out);
  // _74373 _74373_2: pin names not known; wires that end beside it: 1'b0, not_7_out, _74244_2_p4[3], _74244_2_p4[2], _74244_2_p4[1], _74244_2_p4[0], 1'b1, 1'b1, 1'b1, 1'b1, 1'b1, 1'b0, _74373_2_p13[3], _74373_2_p13[2], _74373_2_p13[1], _74373_2_p13[0]
  not not_10 (not_10_out, _74154_1_p16);
  LED led_13 (.in(_74373_2_p13[3]));
  LED led_14 (.in(_74373_2_p13[2]));
  LED led_15 (.in(_74373_2_p13[1]));
  LED led_16 (.in(_74373_2_p13[0]));
  assign _74244_2_p4 = ~_74139_1_p15 ? _74373_2_p13 : 4'bz;  // DriverInvSel driverinvsel_25
  not not_11 (not_11_out, _74244_2_p6);
  not not_12 (not_12_out, _74244_2_p7);
  not not_13 (not_13_out, _74244_2_p8);
  not not_14 (not_14_out, _74244_2_p9);
  LED led_17 (.in(or_4_out));
  // _74244 _74244_4: pin names not known; wires that end beside it: xor_5_out, xor_6_out, xor_7_out, xor_8_out, _74154_1_p14, not_11_out, not_12_out, not_13_out, not_14_out, _74154_1_p15, _74244_4_p11, _74244_4_p12, _74244_4_p13, _74244_4_p14, _74244_4_p15, _74244_4_p16, _74244_4_p13, _74244_4_p14, _74244_4_p15, _74244_4_p16
  PullUp pullup_11 (.out(driverinvsel_7_out));
  // _74244 _74244_5: pin names not known; wires that end beside it: in_5, in_6, in_7, in_8, _74154_1_p16, _74244_2_p4[3], _74244_2_p4[2], _74244_2_p4[1], _74244_2_p4[0], not_10_out, 1'b1, 1'b0, _74244_5_p13, _74244_5_p14, _74244_5_p15, _74244_5_p16, _74244_5_p13, _74244_5_p14, _74244_5_p15, _74244_5_p16
  not not_15 (not_15_out, driverinvsel_7_out);
  PullDown pulldown_12 (.out(_74244_4_p12));
  assign driver_4_out = not_10_out ? not_10_out : 1'bz;  // Driver driver_4
  assign driver_4_out = _74154_1_p16 ? not_8_out : 1'bz;  // Driver driver_5
  // _74175 _74175_7: pin names not known; wires that end beside it: not_15_out, _74154_1_p18, _74244_4_p13, _74244_4_p14, _74244_4_p15, _74244_4_p16, _74244_4_p11, _74244_4_p12, _74244_2_p6, _74244_2_p7, _74244_2_p8, _74244_2_p9
  PullUp pullup_12 (.out(_74244_4_p11));
  PullUp pullup_13 (.out(driver_4_out));
  // _74373 _74373_3: pin names not known; wires that end beside it: 1'b0, driver_4_out, _74244_5_p13, _74244_5_p14, _74244_5_p15, _74244_5_p16, 1'b1, 1'b1, 1'b1, 1'b1, 1'b1, 1'b0, _74373_3_p13[3], _74373_3_p13[2], _74373_3_p13[1], _74373_3_p13[0]
  LED led_18 (.in(_74373_3_p13[3]));
  LED led_19 (.in(_74373_3_p13[2]));
  LED led_20 (.in(_74373_3_p13[1]));
  LED led_21 (.in(_74373_3_p13[0]));
  assign _74244_2_p4 = ~_74139_1_p16 ? _74373_3_p13 : 4'bz;  // DriverInvSel driverinvsel_26

  // Notes on the sheet:
  //   in_9: pin sdfs, default 1
endmodule
