// Digital circuit ALU.dig as structural Verilog
module ALU (
  input  IN1,
  input  IN2,
  input  IN3,
  input  IN4,
  input  IN5,
  input  IN6,
  input  IN7,
  input  IN8,
  input  ADD,
  input  CMP,
  input  SUB,
  input  CPL,
  input  CMP_BIT,
  input  CMP_SEL_1,
  input  CMP_SEL_2,
  output CARRY_FLAG,
  output Q0_out,
  output Q1_out,
  output Q2_out,
  output Q3_out,
  output NOTEqual_FLAG,
  output N_FLAG
);

  wire _74139_1_p1, _74139_1_p9, _74139_1_p10, _74139_1_p11, _74139_1_p12, and_1_out, and_2_out, and_3_out,
       and_4_out, and_5_out, and_6_out, and_7_out, and_8_out, and_9_out, and_10_out, and_11_out, and_12_out,
       and_13_out, and_14_out, and_15_out, and_16_out, delay_1_out, delay_2_out, nor_1_out, not_1_out,
       not_2_out, not_3_out, not_4_out, not_6_out, not_7_out, or_1_out, or_2_out, or_3_out, or_5_out,
       or_6_out, xnor_1_out, xnor_2_out, xnor_3_out, xnor_4_out, xor_1_out, xor_2_out, xor_3_out, xor_4_out,
       xor_5_out, xor_6_out, xor_7_out, xor_8_out, xor_9_out, xor_10_out, xor_11_out;

  not not_1 (not_1_out, IN3);
  not not_2 (not_2_out, IN4);
  not not_3 (not_3_out, IN1);
  not not_4 (not_4_out, IN2);
  // _74139 _74139_1: pin names not known; wires that end beside it: _74139_1_p1, CMP_SEL_1, CMP_SEL_2, 1'b1, 1'b1, 1'b1, 1'b1, 1'b0, _74139_1_p9, _74139_1_p10, _74139_1_p11, _74139_1_p12
  xor xor_1 (xor_1_out, SUB, IN1);
  xor xor_2 (xor_2_out, SUB, IN2);
  xor xor_3 (xor_3_out, SUB, IN3);
  xor xor_4 (xor_4_out, SUB, IN4);
  xnor xnor_1 (xnor_1_out, IN1, IN5);
  xnor xnor_2 (xnor_2_out, IN2, IN6);
  xnor xnor_3 (xnor_3_out, IN3, IN7);
  xnor xnor_4 (xnor_4_out, IN4, IN8);
  xor xor_5 (xor_5_out, xor_1_out, IN5);
  and and_1 (and_1_out, xor_1_out, IN5);
  xor xor_6 (xor_6_out, xor_2_out, IN6);
  and and_2 (and_2_out, xor_2_out, IN6);
  xor xor_7 (xor_7_out, xor_3_out, IN7);
  and and_3 (and_3_out, xor_3_out, IN7);
  xor xor_8 (xor_8_out, xor_4_out, IN8);
  and and_4 (and_4_out, xor_4_out, IN8);
  xor xor_9 (xor_9_out, SUB, xor_5_out);
  and and_5 (and_5_out, SUB, xor_5_out);
  PullDown pulldown_1 (.out(SUB));
  xor xor_10 (xor_10_out, or_1_out, xor_6_out);
  and and_6 (and_6_out, or_1_out, xor_6_out);
  xor xor_11 (xor_11_out, or_2_out, xor_7_out);
  and and_7 (and_7_out, or_2_out, xor_7_out);
  xor xor_12 (N_FLAG, or_3_out, xor_8_out);
  and and_8 (and_8_out, or_3_out, xor_8_out);
  and and_9 (and_9_out, xnor_1_out, xnor_2_out);
  and and_10 (and_10_out, xnor_3_out, xnor_4_out);
  or or_1 (or_1_out, and_5_out, and_1_out);
  or or_2 (or_2_out, and_6_out, and_2_out);
  or or_3 (or_3_out, and_7_out, and_3_out);
  or or_4 (CARRY_FLAG, and_8_out, and_4_out);
  and and_11 (and_11_out, and_9_out, and_10_out);
  and and_12 (and_12_out, xnor_1_out, ~_74139_1_p9);  // And
  and and_13 (and_13_out, xnor_2_out, ~_74139_1_p10);  // And
  and and_14 (and_14_out, xnor_3_out, ~_74139_1_p11);  // And
  and and_15 (and_15_out, xnor_4_out, ~_74139_1_p12);  // And
  not not_5 (_74139_1_p1, CMP_BIT);
  and and_16 (and_16_out, CMP, and_11_out);
  or or_5 (or_5_out, and_12_out, and_13_out, and_16_out, and_14_out, and_15_out);
  not not_6 (not_6_out, CPL);
  not not_7 (not_7_out, or_5_out);
  or or_6 (or_6_out, delay_1_out, delay_2_out);
  Delay #(.delayTime(4)) delay_1 (.in(CMP_BIT), .out(delay_1_out));
  Delay #(.delayTime(2)) delay_2 (.in(CMP), .out(delay_2_out));
  nor nor_1 (nor_1_out, SUB, ADD);
  // _74244 _74244_1: pin names not known; wires that end beside it: 1'b1, 1'b0, xor_9_out, not_3_out, xor_10_out, not_4_out, xor_11_out, not_1_out, N_FLAG, not_2_out, nor_1_out, not_6_out, Q0_out, Q0_out, Q1_out, Q1_out, Q2_out, Q2_out, Q3_out, Q3_out
  and and_17 (NOTEqual_FLAG, not_7_out, or_6_out);
endmodule
