// Digital circuit CPU_FOR_MIT_V2.dig as structural Verilog
module CPU_FOR_MIT_V2 (
  input  clk
);

  wire _74139_1_p1, _74139_1_p2, _74139_1_p3, _74139_1_p4, _74189_1_p4, _74189_1_p5, _74189_1_p6,
       _74189_1_p7, _74189_1_p8, insrutruction_decoder_1_p2, insrutruction_decoder_1_p3,
       insrutruction_decoder_1_p4;

  // Insrutruction_Decoder insrutruction_decoder_1: pin names not known; wires that end beside it: clk, insrutruction_decoder_1_p2, insrutruction_decoder_1_p3, insrutruction_decoder_1_p4
  // _74139 _74139_1: pin names not known; wires that end beside it: _74139_1_p1, _74139_1_p2, _74139_1_p3, _74139_1_p4
  // _74189 _74189_1: pin names not known; wires that end beside it: insrutruction_decoder_1_p2, insrutruction_decoder_1_p3, insrutruction_decoder_1_p4, _74189_1_p4, _74189_1_p5, _74189_1_p6, _74189_1_p7, _74189_1_p8, _74139_1_p3, _74139_1_p1, 1'b1, 1'b0, _74189_1_p5, _74189_1_p6, _74189_1_p7, _74189_1_p8
  // _74189 _74189_2: pin names not known; wires that end beside it: insrutruction_decoder_1_p2, insrutruction_decoder_1_p3, insrutruction_decoder_1_p4, _74189_1_p4, _74189_1_p5, _74189_1_p6, _74189_1_p7, _74189_1_p8, _74139_1_p4, _74139_1_p2, 1'b1, 1'b0, _74189_1_p5, _74189_1_p6, _74189_1_p7, _74189_1_p8
  PullDown pulldown_1 (.out(_74189_1_p5));
  PullDown pulldown_2 (.out(_74189_1_p6));
  PullDown pulldown_3 (.out(_74189_1_p7));
  PullDown pulldown_4 (.out(_74189_1_p8));
endmodule
