// Digital circuit CPU_FOR_MIT_V3.dig as structural Verilog
module CPU_FOR_MIT_V3 (
  input  clk,
  input  in_2,
  input  in_3,
  input  in_4,
  input  in_5,
  input  in_6,
  input  in_7,
  input  in_8,
  input  in_9,
  input  in_10,
  input  in_11,
  input  in_12,
  input  in_13,
  input  in_14,
  input  in_15,
  input  in_16,
  input  in_17,
  input  in_18,
  input  in_19,
  input  in_20,
  input  in_21,
  input  in_22,
  input  in_23,
  input  in_24,
  input  in_25
);

  wire _7448_1_p10, _7448_1_p11, _7448_1_p12, _7448_1_p13, _7448_1_p14, _7448_1_p15, _7448_1_p16,
       _74138_1_p9, _74138_1_p10, _74138_1_p11, _74138_1_p12, _74138_1_p13, _74138_2_p9, _74138_2_p10,
       _74138_2_p11, _74175_1_p9, _74175_1_p10, _74175_1_p11, _74175_1_p12, _74189_1_p13, _74189_1_p14,
       _74189_1_p15, _74189_1_p16, _74191_2_p11, _74191_4_p11, _74191_5_p11, _74248_1_p3, _74248_1_p4,
       _74248_1_p5, _74248_1_p6, _74248_1_p10, _74248_1_p11, _74248_1_p12, _74248_1_p13, _74248_1_p14,
       _74248_1_p15, _74248_1_p16, _74373_1_p19, _74373_1_p20, _74373_1_p21, _74373_1_p22, _74373_1_p23,
       _74373_1_p24, _74373_2_pin19, _74373_2_pin20, _74373_3_p19, _74373_3_p20, _74373_3_p21, _74373_3_p22,
       _74373_3_p23, _74373_3_p24, _74373_4_pin12, _74373_4_pin13, _74373_4_pin19, _74373_4_pin20,
       _74373_5_pin19, _74373_5_pin20, _74373_6_p13, _74373_6_p14, _74373_6_p15, _74373_6_p16, _74373_8_p13,
       _74373_8_p14, _74373_8_p15, _74373_9_p13, _74373_9_p14, _74373_9_p15, _74373_10_p13, _74373_10_p14,
       _74373_10_p15, _74373_10_p16, _744017_1_p6, _744017_1_p7, alu_1_carry_flag, alu_1_n_flag,
       alu_1_notequal_flag, and_1_out, and_2_out, and_3_out, and_5_out, and_6_out, and_7_out, and_9_out,
       and_10_out, and_11_out, clock2, clock3_1, clock3_2, delay_1_out, nand_1_out, nor_1_out, not_1_out,
       not_2_out, not_3_out, not_4_out, not_5_out, not_6_out, not_7_out, not_8_out, not_9_out, not_10_out,
       not_11_out, not_12_out, not_13_out, not_14_out, not_15_out, not_16_out, not_17_out, not_18_out,
       or_1_out, or_2_out, or_3_out, or_4_out, or_5_out, or_6_out, or_7_out, or_8_out, or_9_out,
       pulldown_8_out, pulldown_9_out, pullup_1_out, pullup_2_out;
  wire [2:0] rom_2_d_2;
  wire [3:0] driver_1_out, pulldown_1_out, rom_1_d, rom_3_d;
  wire [9:0] d_ff_2_q;
  wire [11:0] _74191_4_p12;
  wire [31:0] rom_2_d;

  and and_1 (and_1_out, not_2_out, ~or_8_out);  // And
  not not_1 (not_1_out, or_8_out);
  ROM #(.AddrBits(3), .Bits(4)) rom_1 (.A(rom_2_d_2), .sel(1'b1), .D(rom_1_d));
  and and_2 (and_2_out, and_3_out, ~or_8_out);  // And
  or or_1 (or_1_out, 1'b0, rom_2_d[31]);
  assign driver_1_out = or_1_out ? rom_1_d : 4'bz;  // Driver driver_1
  or or_2 (or_2_out, rom_2_d[6], _744017_1_p7);
  PullDown pulldown_1 (.out(pulldown_1_out[0]));
  assign pulldown_1_out = not_1_out ? driver_1_out : 4'bz;  // Driver driver_2
  PullDown pulldown_2 (.out(pulldown_1_out[1]));
  PullDown pulldown_3 (.out(pulldown_1_out[2]));
  not not_2 (not_2_out, _744017_1_p6);
  // _74191 _74191_1: pin names not known; wires that end beside it: 1'b0, 1'b0, 1'b0, 1'b0, 1'b1, 1'b0, and_2_out, 1'b0, 1'b0, clock2, d_ff_2_q[0], d_ff_2_q[1], d_ff_2_q[2]
  // _74191 _74191_2: pin names not known; wires that end beside it: pulldown_1_out[0], pulldown_1_out[1], pulldown_1_out[2], pulldown_1_out[3], 1'b1, 1'b0, and_1_out, 1'b0, 1'b0, 1'b0, _74191_2_p11, d_ff_2_q[3], d_ff_2_q[4], d_ff_2_q[5], d_ff_2_q[6]
  PullDown pulldown_4 (.out(pulldown_1_out[3]));
  // _744017 _744017_1: pin names not known; wires that end beside it: 1'b1, 1'b0, 1'b0, clock3_1, or_2_out, _744017_1_p6, _744017_1_p7
  and and_3 (and_3_out, nand_1_out, not_3_out);
  nand nand_1 (nand_1_out, d_ff_2_q[2], d_ff_2_q[1], d_ff_2_q[0]);
  and and_4 (d_ff_2_q[7], clock3_1, _74191_2_p11);
  PullDown pulldown_5 (.out(driver_1_out[3]));
  // _74191 _74191_3: pin names not known; wires that end beside it: 1'b0, 1'b0, 1'b0, 1'b0, 1'b1, 1'b0, and_3_out, 1'b0, 1'b0, clk, clock3_1
  not not_3 (not_3_out, rom_2_d[6]);
  D_FF d_ff_1 (.D(pulldown_8_out), .C(delay_1_out), .Q(d_ff_2_q[8]));  // open: nQ
  D_FF d_ff_2 (.D(pulldown_9_out), .C(delay_1_out), .Q(d_ff_2_q[9]));  // open: nQ
  PullDown pulldown_6 (.out(driver_1_out[2]));
  PullDown pulldown_7 (.out(driver_1_out[1]));
  PullDown pulldown_8 (.out(pulldown_8_out));
  PullDown pulldown_9 (.out(pulldown_9_out));
  ROM #(.AddrBits(10), .Bits(32)) rom_2 (.A(d_ff_2_q), .sel(1'b1), .D({rom_2_d[31], rom_2_d_2, rom_2_d[27:0]}));
  PullDown pulldown_10 (.out(driver_1_out[0]));
  or or_3 (or_3_out, or_8_out, rom_2_d[6]);
  Delay #(.delayTime(4)) delay_1 (.in(or_3_out), .out(delay_1_out));
  and and_5 (and_5_out, clk, clk);
  and and_6 (and_6_out, and_5_out, and_5_out);
  and and_7 (and_7_out, and_6_out, and_6_out);
  not not_4 (not_4_out, rom_2_d[21]);
  not not_5 (not_5_out, rom_2_d[22]);
  // _74373 _74373_1: pin names not known; wires that end beside it: 1'b0, rom_2_d[8], driver_1_out[0], driver_1_out[1], driver_1_out[2], driver_1_out[3], 1'b0, 1'b0, 1'b0, 1'b0, 1'b1, 1'b0, rom_2_d[7], driver_1_out[1], driver_1_out[3], 1'b0, 1'b0, 1'b0, _74373_1_p19, _74373_1_p20, _74373_1_p21, _74373_1_p22, _74373_1_p23, _74373_1_p24
  _74373 _74373_2 (
    .pin1(1'b0), .pin2(driver_1_out[0]), .pin3(driver_1_out[2]), .pin4(1'b1), .pin5(1'b0), .pin6(1'b1),
    .pin19(_74373_2_pin19), .pin20(_74373_2_pin20));  // open: pin7, pin8, pin9, pin10, pin11, pin12, pin13, pin14, pin15, pin16, pin17, pin18
  Delay #(.delayTime(3)) delay_2 (.in(clock3_1), .out(clock3_2));
  and and_8 (clock2, and_7_out, and_7_out);
  not not_6 (not_6_out, rom_2_d[19]);
  not not_7 (not_7_out, rom_2_d[20]);
  ALU alu_1 (
    .IN1(_74373_1_p19), .IN2(_74373_1_p20), .IN3(_74373_1_p21), .IN4(_74373_1_p22), .IN5(_74373_2_pin20),
    .IN6(_74373_1_p23), .IN7(_74373_2_pin19), .IN8(_74373_1_p24), .ADD(rom_2_d[9]), .CMP(rom_2_d[15]),
    .SUB(rom_2_d[10]), .CPL(rom_2_d[11]), .CMP_BIT(rom_2_d[23]), .CMP_SEL_1(driver_1_out[0]),
    .CMP_SEL_2(driver_1_out[1]), .CARRY_FLAG(alu_1_carry_flag), .Q0_out(driver_1_out[0]),
    .Q1_out(driver_1_out[1]), .Q2_out(driver_1_out[2]), .Q3_out(driver_1_out[3]),
    .NOTEqual_FLAG(alu_1_notequal_flag), .N_FLAG(alu_1_n_flag));
  or or_4 (or_4_out, rom_2_d[11], rom_2_d[10], rom_2_d[9], rom_2_d[15]);
  or or_5 (or_5_out, rom_2_d[15], rom_2_d[11], rom_2_d[19], rom_2_d[21], rom_2_d[22]);
  // _74373 _74373_3: pin names not known; wires that end beside it: 1'b0, rom_2_d[5], driver_1_out[0], driver_1_out[1], driver_1_out[2], driver_1_out[3], 1'b0, 1'b0, 1'b0, 1'b0, 1'b1, 1'b0, rom_2_d[14], driver_1_out[1], driver_1_out[3], 1'b0, 1'b0, 1'b0, _74373_3_p19, _74373_3_p20, _74373_3_p21, _74373_3_p22, _74373_3_p23, _74373_3_p24
  _74373 _74373_4 (
    .pin1(1'b0), .pin2(driver_1_out[0]), .pin3(driver_1_out[2]), .pin4(1'b0), .pin5(1'b0), .pin6(1'b1),
    .pin8(rom_2_d[27]), .pin9(driver_1_out[1]), .pin10(driver_1_out[3]), .pin12(_74373_4_pin12),
    .pin13(_74373_4_pin13), .pin19(_74373_4_pin19), .pin20(_74373_4_pin20));  // open: pin7, pin11, pin14, pin15, pin16, pin17, pin18
  _74373 _74373_5 (
    .pin1(1'b0), .pin2(driver_1_out[0]), .pin3(driver_1_out[2]), .pin4(1'b0), .pin5(1'b0), .pin6(1'b1),
    .pin19(_74373_5_pin19), .pin20(_74373_5_pin20));  // open: pin7, pin8, pin9, pin10, pin11, pin12, pin13, pin14, pin15, pin16, pin17, pin18
  or or_6 (or_6_out, rom_2_d[2], rom_2_d[20], rom_2_d[25], rom_2_d[12], rom_2_d[31]);
  or or_7 (or_7_out, or_6_out, rom_2_d[9], rom_2_d[4], rom_2_d[10], or_5_out);
  nor nor_1 (nor_1_out, rom_2_d[6], alu_1_notequal_flag);
  // _74191 _74191_4: pin names not known; wires that end beside it: _74373_3_p19, _74373_3_p20, _74373_3_p21, _74373_3_p22, 1'b1, 1'b0, nor_1_out, 1'b0, 1'b0, clock3_2, _74191_4_p11, _74191_4_p12[0], _74191_4_p12[1], _74191_4_p12[2], _74191_4_p12[3]
  // _74191 _74191_5: pin names not known; wires that end beside it: _74373_4_pin20, _74373_3_p23, _74373_4_pin19, _74373_3_p24, 1'b1, 1'b0, nor_1_out, 1'b0, _74191_4_p11, clock3_2, _74191_5_p11, _74191_4_p12[4], _74191_4_p12[5], _74191_4_p12[6], _74191_4_p12[7]
  not not_8 (not_8_out, rom_2_d[6]);
  // _74191 _74191_6: pin names not known; wires that end beside it: _74373_5_pin20, _74373_4_pin13, _74373_5_pin19, _74373_4_pin12, 1'b1, 1'b0, not_8_out, 1'b0, _74191_5_p11, clock3_2, _74191_4_p12[8], _74191_4_p12[9], _74191_4_p12[10], _74191_4_p12[11]
  // _74373 _74373_6: pin names not known; wires that end beside it: 1'b1, 1'b0, 1'b0, driver_1_out[0], driver_1_out[1], driver_1_out[2], driver_1_out[3], 1'b0, 1'b0, 1'b0, 1'b0, rom_2_d[13], _74373_6_p13, _74373_6_p14, _74373_6_p15, _74373_6_p16
  // _74244 _74244_1: pin names not known; wires that end beside it: driver_1_out[0], _74191_4_p12[0], driver_1_out[1], _74191_4_p12[1], driver_1_out[2], _74191_4_p12[2], driver_1_out[3], _74191_4_p12[3], driver_1_out[0], not_4_out, driver_1_out[1], _74191_4_p12[4], driver_1_out[2], _74191_4_p12[5], driver_1_out[3], _74191_4_p12[6], _74191_4_p12[7], not_5_out, 1'b1, 1'b0
  not not_9 (not_9_out, rom_2_d[1]);
  // _74189 _74189_1: pin names not known; wires that end beside it: _74373_6_p13, _74373_6_p14, _74373_6_p15, _74373_6_p16, driver_1_out[0], driver_1_out[1], driver_1_out[2], driver_1_out[3], not_9_out, 1'b0, 1'b1, 1'b0, _74189_1_p13, _74189_1_p14, _74189_1_p15, _74189_1_p16
  ROM #(.AddrBits(12), .isProgramMemory("true"), .Bits(4)) rom_3 (.A(_74191_4_p12), .sel(1'b1), .D(rom_3_d));
  not not_10 (not_10_out, _74189_1_p13);
  not not_11 (not_11_out, _74189_1_p14);
  not not_12 (not_12_out, _74189_1_p15);
  not not_13 (not_13_out, _74189_1_p16);
  not not_14 (not_14_out, rom_2_d[2]);
  not not_15 (not_15_out, rom_2_d[4]);
  // _74244 _74244_2: pin names not known; wires that end beside it: rom_3_d[0], rom_3_d[1], rom_3_d[2], rom_3_d[3], or_7_out, not_10_out, not_11_out, not_12_out, not_13_out, not_14_out, 1'b1, 1'b0, driver_1_out[0], driver_1_out[1], driver_1_out[2], driver_1_out[3], driver_1_out[0], driver_1_out[1], driver_1_out[2], driver_1_out[3]
  // _74373 _74373_7: pin names not known; wires that end beside it: 1'b1, 1'b0, not_15_out, driver_1_out[0], driver_1_out[1], driver_1_out[2], driver_1_out[3], 1'b0, 1'b0, 1'b0, 1'b0, rom_2_d[3], driver_1_out[0], driver_1_out[1], driver_1_out[2], driver_1_out[3]
  // _74373 _74373_8: pin names not known; wires that end beside it: 1'b1, 1'b0, 1'b0, driver_1_out[0], driver_1_out[1], driver_1_out[2], 1'b0, 1'b0, 1'b0, 1'b0, 1'b0, rom_2_d[26], _74373_8_p13, _74373_8_p14, _74373_8_p15
  PullUp pullup_1 (.out(pullup_1_out));
  // _74373 _74373_9: pin names not known; wires that end beside it: 1'b1, 1'b0, 1'b0, driver_1_out[0], driver_1_out[1], driver_1_out[2], 1'b0, 1'b0, 1'b0, 1'b0, 1'b0, rom_2_d[26], _74373_9_p13, _74373_9_p14, _74373_9_p15
  PullUp pullup_2 (.out(pullup_2_out));
  // _74138 _74138_1: pin names not known; wires that end beside it: 1'b1, 1'b0, rom_2_d[25], 1'b0, 1'b0, _74373_8_p13, _74373_8_p14, _74373_8_p15, _74138_1_p9, _74138_1_p10, _74138_1_p11, _74138_1_p12, _74138_1_p13
  // _74138 _74138_2: pin names not known; wires that end beside it: 1'b1, 1'b0, rom_2_d[24], 1'b0, 1'b0, _74373_9_p13, _74373_9_p14, _74373_9_p15, _74138_2_p9, _74138_2_p10, _74138_2_p11
  not not_16 (not_16_out, _74138_2_p9);
  not not_17 (not_17_out, _74138_2_p10);
  not not_18 (not_18_out, _74138_2_p11);
  // _74175 _74175_1: pin names not known; wires that end beside it: driver_1_out[0], driver_1_out[1], driver_1_out[2], driver_1_out[3], not_16_out, 1'b1, 1'b1, 1'b0, _74175_1_p9, _74175_1_p10, _74175_1_p11, _74175_1_p12
  // _7448 _7448_1: pin names not known; wires that end beside it: 1'b1, 1'b0, _74175_1_p9, _74175_1_p10, _74175_1_p11, _74175_1_p12, pullup_1_out, 1'b1, 1'b1, _7448_1_p10, _7448_1_p11, _7448_1_p12, _7448_1_p13, _7448_1_p14, _7448_1_p15, _7448_1_p16
  // _74248 _74248_1: pin names not known; wires that end beside it: 1'b1, 1'b0, _74248_1_p3, _74248_1_p4, _74248_1_p5, _74248_1_p6, pullup_2_out, 1'b1, 1'b1, _74248_1_p10, _74248_1_p11, _74248_1_p12, _74248_1_p13, _74248_1_p14, _74248_1_p15, _74248_1_p16
  // _74175 _74175_2: pin names not known; wires that end beside it: driver_1_out[0], driver_1_out[1], driver_1_out[2], driver_1_out[3], not_17_out, 1'b1, 1'b1, 1'b0, _74248_1_p3, _74248_1_p4, _74248_1_p5, _74248_1_p6
  assign driver_1_out[0] = ~_74138_1_p9 ? in_6 : 1'bz;  // DriverInvSel driverinvsel_1
  assign driver_1_out[1] = ~_74138_1_p9 ? in_7 : 1'bz;  // DriverInvSel driverinvsel_2
  assign driver_1_out[2] = ~_74138_1_p9 ? in_8 : 1'bz;  // DriverInvSel driverinvsel_3
  assign driver_1_out[3] = ~_74138_1_p9 ? in_9 : 1'bz;  // DriverInvSel driverinvsel_4
  Seven_Seg seven_seg_1 (
    .a(_74248_1_p10), .b(_74248_1_p11), .c(_74248_1_p12), .d(_74248_1_p13), .e(_74248_1_p14),
    .f(_74248_1_p15), .g(_74248_1_p16), .dp(1'b0));
  Seven_Seg seven_seg_2 (
    .a(_7448_1_p10), .b(_7448_1_p11), .c(_7448_1_p12), .d(_7448_1_p13), .e(_7448_1_p14), .f(_7448_1_p15),
    .g(_7448_1_p16), .dp(1'b0));
  assign driver_1_out[0] = ~_74138_1_p10 ? in_2 : 1'bz;  // DriverInvSel driverinvsel_5
  assign driver_1_out[1] = ~_74138_1_p10 ? in_3 : 1'bz;  // DriverInvSel driverinvsel_6
  assign driver_1_out[2] = ~_74138_1_p10 ? in_4 : 1'bz;  // DriverInvSel driverinvsel_7
  assign driver_1_out[3] = ~_74138_1_p10 ? in_5 : 1'bz;  // DriverInvSel driverinvsel_8
  assign driver_1_out[0] = ~_74138_1_p11 ? in_10 : 1'bz;  // DriverInvSel driverinvsel_9
  assign driver_1_out[1] = ~_74138_1_p11 ? in_11 : 1'bz;  // DriverInvSel driverinvsel_10
  assign driver_1_out[2] = ~_74138_1_p11 ? in_12 : 1'bz;  // DriverInvSel driverinvsel_11
  assign driver_1_out[3] = ~_74138_1_p11 ? in_13 : 1'bz;  // DriverInvSel driverinvsel_12
  Seven_Seg seven_seg_3 (.a(in_18), .b(in_19), .c(in_20), .d(in_21), .e(in_22), .f(in_23), .g(in_24), .dp(in_25));
  assign driver_1_out[0] = ~_74138_1_p12 ? in_14 : 1'bz;  // DriverInvSel driverinvsel_13
  assign driver_1_out[1] = ~_74138_1_p12 ? in_15 : 1'bz;  // DriverInvSel driverinvsel_14
  assign driver_1_out[2] = ~_74138_1_p12 ? in_16 : 1'bz;  // DriverInvSel driverinvsel_15
  assign driver_1_out[3] = ~_74138_1_p12 ? in_17 : 1'bz;  // DriverInvSel driverinvsel_16
  // _74373 _74373_10: pin names not known; wires that end beside it: 1'b1, 1'b0, 1'b0, driver_1_out[0], driver_1_out[1], driver_1_out[2], driver_1_out[3], 1'b0, 1'b0, 1'b0, 1'b0, not_18_out, _74373_10_p13, _74373_10_p14, _74373_10_p15, _74373_10_p16
  PullDown pulldown_11 (.out(_74373_10_p16));
  PullDown pulldown_12 (.out(_74373_10_p14));
  and and_9 (and_9_out, in_14, _74373_10_p13);
  and and_10 (and_10_out, in_15, _74373_10_p14);
  and and_11 (and_11_out, in_16, _74373_10_p15);
  PullDown pulldown_13 (.out(_74373_10_p15));
  // _74373 _74373_11: pin names not known; wires that end beside it: 1'b1, 1'b0, _74138_1_p13, alu_1_carry_flag, alu_1_n_flag, 1'b0, 1'b0, 1'b0, 1'b0, 1'b0, 1'b0, or_4_out, driver_1_out[0], driver_1_out[1], driver_1_out[2], driver_1_out[3]
  or or_8 (or_8_out, and_9_out, and_10_out, and_11_out);
  or or_9 (or_9_out, and_9_out, and_11_out);
  assign pulldown_9_out = or_8_out ? or_9_out : 1'bz;  // Driver driver_3
  assign pulldown_8_out = or_8_out ? and_10_out : 1'bz;  // Driver driver_4

  // Notes on the sheet:
  //   clk: Hz: 200
  //   contents of rom_1 (hex, n*v repeats v):
  //   4,c0,6*0,8
  //   contents of rom_2 (hex, n*v repeats v):
  //   9*0,2000,0,2,5*0,2000,c,2000,0,12,0,0,0,20,0,4000,420000,8000000
  //   ,210000,40,0,2000,84,2000,104,2000,202,0,0,2000,104,2000,84,2000
  //   ,402,0,0,20,0,4000,0,2000,104,8000,0,2000,84,2000,802,4*0,164000
  //   ,d0020,40,5*0,20,84000000,4000,0,2000100,0,800000,0,4000000,0
  //   ,1000000,5*0,4000000,0,4000000,3000000,4*0,2000,0,4000000,1000004
  //   ,4*0,2000,84,2000,104,4*0,4000000,0,2000,2000002,139*0,90000020
  //   ,a0004000,40,253*0,b0000020,c0004000,40,253*0,d0000020,e0004000,40
  //   contents of rom_3 (hex, n*v repeats v):
  //   3
endmodule
