// Digital circuit Insrutruction_Decoder.dig as structural Verilog
module Insrutruction_Decoder (
  input  D0,
  input  D1,
  input  D2,
  input  D3,
  input  Clock,
  output I0,
  output I1,
  output I2,
  output I3,
  output A0,
  output A1,
  output A2,
  output A3,
  output Q0,
  output Q1,
  output Q2,
  output Q3,
  output I4,
  output I5,
  output I6,
  output I7,
  output I8,
  output I9,
  output I10,
  output I11,
  output I12,
  output I13,
  output I14,
  output I15,
  output L0,
  output L1,
  output L2,
  output L3,
  output L4
);

  wire _74175_1_p9, _74175_1_p10, _74175_1_p11, _74175_1_p12, _744017_1_p5, or_1_out, or_2_out;

  // _744017 _744017_1: pin names not known; wires that end beside it: 1'b1, 1'b0, 1'b0, Clock, _744017_1_p5, L0, L1, L2, L3, L4, _744017_1_p5
  or or_1 (or_1_out, L1, L3);
  or or_2 (or_2_out, L2, L4);
  // _74175 _74175_1: pin names not known; wires that end beside it: D0, D1, D2, D3, L0, 1'b1, 1'b1, 1'b0, _74175_1_p9, _74175_1_p10, _74175_1_p11, _74175_1_p12
  // _74175 _74175_2: pin names not known; wires that end beside it: D0, D1, D2, D3, or_1_out, 1'b1, 1'b1, 1'b0, A0, A1, A2, A3
  // _74175 _74175_3: pin names not known; wires that end beside it: D0, D1, D2, D3, or_2_out, 1'b1, 1'b1, 1'b0, Q0, Q1, Q2, Q3
  // _74154 _74154_1: pin names not known; wires that end beside it: 1'b1, 1'b0, 1'b1, 1'b1, _74175_1_p9, _74175_1_p10, _74175_1_p11, _74175_1_p12, I0, I1, I2, I3, I4, I5, I6, I7, I8, I9, I10, I11, I12, I13, I14, I15
endmodule
