// Digital circuit Instruction_decoder_v2.dig as structural Verilog
module Instruction_decoder_v2 (
  input  D0,
  input  D1,
  input  D2,
  input  D3,
  input  c,
  output _1T0,
  output _1T1,
  output _1T2,
  output _1T3,
  output _1T4,
  output _1T5,
  output _1T6,
  output _1T7,
  output _1T8,
  output _1T9,
  output _1T10,
  output _1T11,
  output _1T12,
  output _1T13,
  output _1T14,
  output _1T15,
  output _2T0,
  output _3T0,
  output _2T1,
  output _2T2,
  output _2T3,
  output _2T4,
  output _2T5,
  output _2T6,
  output _2T7,
  output _2T8,
  output _2T9,
  output _2T10,
  output _2T11,
  output _2T12,
  output _2T13,
  output _2T14,
  output _2T15,
  output _3T1,
  output _3T2,
  output _3T3,
  output _3T4,
  output _3T5,
  output _3T6,
  output _3T7,
  output _3T8,
  output _3T9,
  output _3T10,
  output _3T11,
  output _3T12,
  output _3T13,
  output _3T14,
  output _3T15
);

  wire _74154_1_p19, _74154_1_p20, _74154_1_p21, _74154_1_p22, _74154_1_p23, _74154_2_p21, _74154_3_p20,
       _74373_1_p5, _744017_1_p5;

  // _74154 _74154_1: pin names not known; wires that end beside it: _1T15, _1T14, _1T13, _1T12, _1T11, _1T10, _1T9, _1T8, _1T7, _1T6, _1T5, _1T4, _1T3, _1T2, _1T1, _1T0, _2T15, 1'b1, _74154_1_p19, _74154_1_p20, _74154_1_p21, _74154_1_p22, _74154_1_p23, 1'b1, 1'b0, 1'b1
  // _74154 _74154_2: pin names not known; wires that end beside it: _2T14, _2T13, _2T12, _2T11, _2T10, _2T9, _2T8, _2T7, _2T6, _2T5, _2T4, _2T3, _2T2, _2T1, _2T0, _3T15, _74154_1_p19, _74154_1_p20, _74154_1_p21, _74154_1_p22, _74154_2_p21, 1'b1, 1'b0, 1'b1
  // _74154 _74154_3: pin names not known; wires that end beside it: _3T14, _3T13, _3T12, _3T11, _3T10, _3T9, _3T8, _3T7, _3T6, _3T5, _3T4, _3T3, _3T2, _3T1, _3T0, _74154_1_p19, _74154_1_p20, _74154_1_p21, _74154_1_p22, _74154_3_p20, 1'b1, 1'b0, 1'b1
  // _74373 _74373_1: pin names not known; wires that end beside it: _74154_1_p19, _74154_1_p20, _74154_1_p21, _74154_1_p22, _74373_1_p5, 1'b0, 1'b0, 1'b0, 1'b0, D3, D2, D1, D0, 1'b0, 1'b0, 1'b1
  // _744017 _744017_1: pin names not known; wires that end beside it: 1'b1, 1'b0, 1'b0, c, _744017_1_p5, _74373_1_p5, _74154_1_p23, _74154_2_p21, _74154_3_p20, _744017_1_p5
endmodule
