// Digital circuit CPU_FOR_MIT_V1.dig as structural Verilog
module CPU_FOR_MIT_V1 (
  input  clk,
  input  in_2,
  input  in_3,
  input  in_4,
  input  in_5
);

  wire _7493_1_p6, _7493_1_p8, _74154_1_p9, _74189_1_p13, _74189_1_p14, _74189_1_p15, _74189_1_p16,
       _74244_1_p10, _74244_1_p13, _74244_1_p14, _74244_1_p15, _74244_1_p16, _74244_2_p6, _74244_2_p7,
       _74244_2_p8, _74244_2_p9, _74244_2_p13, _74244_2_p14, _74244_2_p15, _74244_2_p16, _74373_1_p19,
       _74373_1_p20, _74373_1_p21, _74373_1_p22, _74373_1_p23, _74373_1_p24, _74373_2_pin12, _74373_2_pin13,
       _74373_2_pin19, _74373_2_pin20, _74373_3_pin19, _74373_3_pin20, _744017_1_p3, _744017_1_p6,
       _744017_1_p7, _744017_1_p8, not_1_out, not_2_out, not_3_out, not_4_out, not_5_out;

  // _7493 _7493_1: pin names not known; wires that end beside it: 1'b0, 1'b0, clk, 1'b1, 1'b0, _7493_1_p6, _7493_1_p6, _7493_1_p8
  // _744017 _744017_1: pin names not known; wires that end beside it: 1'b0, _7493_1_p8, _744017_1_p3, 1'b1, 1'b0, _744017_1_p6, _744017_1_p7, _744017_1_p8, _744017_1_p3
  // _74373 _74373_1: pin names not known; wires that end beside it: 1'b0, _744017_1_p3, in_2, in_3, in_4, in_5, 1'b0, 1'b0, 1'b0, 1'b0, 1'b1, 1'b0, _744017_1_p8, in_3, in_5, 1'b0, 1'b0, 1'b0, _74373_1_p19, _74373_1_p20, _74373_1_p21, _74373_1_p22, _74373_1_p23, _74373_1_p24
  _74373 _74373_2 (
    .pin1(1'b0), .pin2(in_2), .pin3(in_4), .pin4(1'b0), .pin5(1'b0), .pin6(1'b1), .pin8(_744017_1_p7),
    .pin9(in_3), .pin10(in_5), .pin12(_74373_2_pin12), .pin13(_74373_2_pin13), .pin19(_74373_2_pin19),
    .pin20(_74373_2_pin20));  // open: pin7, pin11, pin14, pin15, pin16, pin17, pin18
  _74373 _74373_3 (
    .pin1(1'b0), .pin2(in_2), .pin3(in_4), .pin4(1'b0), .pin5(1'b0), .pin6(1'b1), .pin8(_744017_1_p6),
    .pin9(in_3), .pin10(in_5), .pin19(_74373_3_pin19), .pin20(_74373_3_pin20));  // open: pin7, pin11, pin12, pin13, pin14, pin15, pin16, pin17, pin18
  // _74373 _74373_4: pin names not known; wires that end beside it: 1'b0, 1'b0, 1'b0, 1'b0, in_2, in_4, 1'b0, 1'b0, 1'b0, 1'b0, 1'b1, 1'b0
  // _74154 _74154_1: pin names not known; wires that end beside it: 1'b1, 1'b0, 1'b1, 1'b1, _74373_1_p19, _74373_1_p20, _74373_1_p21, _74373_1_p22, _74154_1_p9
  not not_1 (not_1_out, _74244_1_p10);
  // _74244 _74244_1: pin names not known; wires that end beside it: _74373_2_pin20, _74373_1_p23, _74373_2_pin19, _74373_1_p24, not_1_out, _74373_3_pin20, _74373_2_pin13, _74373_3_pin19, _74373_2_pin12, _74244_1_p10, 1'b1, 1'b0, _74244_1_p13, _74244_1_p14, _74244_1_p15, _74244_1_p16, _74244_1_p13, _74244_1_p14, _74244_1_p15, _74244_1_p16
  // _74244 _74244_2: pin names not known; wires that end beside it: _74373_3_pin20, _74373_2_pin13, _74373_3_pin19, _74373_2_pin12, 1'b0, _74244_2_p6, _74244_2_p7, _74244_2_p8, _74244_2_p9, 1'b1, 1'b1, 1'b0, _74244_2_p13, _74244_2_p14, _74244_2_p15, _74244_2_p16, _74244_2_p13, _74244_2_p14, _74244_2_p15, _74244_2_p16
  // _74189 _74189_1: pin names not known; wires that end beside it: _74244_1_p13, _74244_1_p14, _74244_1_p15, _74244_1_p16, _74244_2_p13, _74244_2_p14, _74244_2_p15, _74244_2_p16, _74154_1_p9, 1'b0, 1'b1, 1'b0, _74189_1_p13, _74189_1_p14, _74189_1_p15, _74189_1_p16
  not not_2 (not_2_out, _74189_1_p13);
  not not_3 (not_3_out, _74189_1_p14);
  not not_4 (not_4_out, _74189_1_p15);
  not not_5 (not_5_out, _74189_1_p16);
  // _74175 _74175_1: pin names not known; wires that end beside it: not_2_out, not_3_out, not_4_out, not_5_out, 1'b1, 1'b1, 1'b0, _74244_2_p6, _74244_2_p7, _74244_2_p8, _74244_2_p9
endmodule
