// Digital circuit Stack_FOR_MIT.dig as structural Verilog
module Stack_FOR_MIT (
  input  D0,
  input  D1,
  input  D2,
  input  D3,
  input  Clock_A,
  input  nPUSH_POP_A,
  input  Clock_B,
  input  Out_A,
  input  Out_B,
  input  Clock_C,
  input  Out_C,
  output Q0,
  output Q1,
  output Q2,
  output Q3
);

  wire _74189_1_p13, _74189_1_p14, _74189_1_p15, _74189_1_p16, _74189_2_p13, _74189_2_p14, _74189_2_p15,
       _74189_2_p16, _74189_3_p13, _74189_3_p14, _74189_3_p15, _74189_3_p16, _74191_1_p11, _74191_1_p12,
       _74191_1_p13, _74191_1_p14, _74244_1_p13, _74244_1_p14, _74244_1_p15, _74244_1_p16, and_1_out,
       not_1_out, not_2_out, not_3_out, not_4_out, xor_1_out, xor_2_out, xor_3_out;

  xor xor_1 (xor_1_out, Out_A, Clock_A);
  // _74191 _74191_1: pin names not known; wires that end beside it: 1'b0, 1'b0, 1'b0, 1'b0, 1'b1, 1'b0, 1'b1, nPUSH_POP_A, 1'b0, xor_1_out, _74191_1_p11, _74191_1_p12, _74191_1_p13, _74191_1_p14
  xor xor_2 (xor_2_out, Out_B, Clock_B);
  xor xor_3 (xor_3_out, Out_C, Clock_C);
  // _74189 _74189_1: pin names not known; wires that end beside it: _74191_1_p11, _74191_1_p12, _74191_1_p13, _74191_1_p14, D0, D1, D2, D3, nPUSH_POP_A, xor_1_out, 1'b1, 1'b0, _74189_1_p13, _74189_1_p14, _74189_1_p15, _74189_1_p16
  // _74189 _74189_2: pin names not known; wires that end beside it: _74191_1_p11, _74191_1_p12, _74191_1_p13, _74191_1_p14, D0, D1, D2, D3, nPUSH_POP_A, xor_2_out, 1'b1, 1'b0, _74189_2_p13, _74189_2_p14, _74189_2_p15, _74189_2_p16
  // _74189 _74189_3: pin names not known; wires that end beside it: _74191_1_p11, _74191_1_p12, _74191_1_p13, _74191_1_p14, D0, D1, D2, D3, nPUSH_POP_A, xor_3_out, 1'b1, 1'b0, _74189_3_p13, _74189_3_p14, _74189_3_p15, _74189_3_p16
  // _74244 _74244_1: pin names not known; wires that end beside it: _74189_1_p13, _74189_1_p14, _74189_1_p15, _74189_1_p16, Out_A, _74189_2_p13, _74189_2_p14, _74189_2_p15, _74189_2_p16, Out_B, 1'b1, 1'b0, _74244_1_p13, _74244_1_p14, _74244_1_p15, _74244_1_p16, _74244_1_p13, _74244_1_p14, _74244_1_p15, _74244_1_p16
  assign _74244_1_p13 = ~Out_C ? _74189_3_p13 : 1'bz;  // DriverInvSel driverinvsel_1
  assign _74244_1_p14 = ~Out_C ? _74189_3_p14 : 1'bz;  // DriverInvSel driverinvsel_2
  assign _74244_1_p15 = ~Out_C ? _74189_3_p15 : 1'bz;  // DriverInvSel driverinvsel_3
  assign _74244_1_p16 = ~Out_C ? _74189_3_p16 : 1'bz;  // DriverInvSel driverinvsel_4
  not not_1 (not_1_out, _74244_1_p13);
  not not_2 (not_2_out, _74244_1_p14);
  not not_3 (not_3_out, _74244_1_p15);
  not not_4 (not_4_out, _74244_1_p16);
  and and_1 (and_1_out, Out_A, Out_B, Out_C);
  assign Q0 = ~and_1_out ? not_1_out : 1'bz;  // DriverInvSel driverinvsel_5
  assign Q1 = ~and_1_out ? not_2_out : 1'bz;  // DriverInvSel driverinvsel_6
  assign Q2 = ~and_1_out ? not_3_out : 1'bz;  // DriverInvSel driverinvsel_7
  assign Q3 = ~and_1_out ? not_4_out : 1'bz;  // DriverInvSel driverinvsel_8

  // Notes on the sheet:
  //   Out_A: default 1
  //   Out_B: default 1
  //   Out_C: default 1
endmodule
