// Digital circuit TEC_2.2.dig as structural Verilog
module TEC_2_2 (
  input  clk,
  input  in_2,
  input  in_3,
  input  in_4
);

  wire _74138_1_p10, _74138_1_p11, _74138_1_p12, _74138_1_p13, _74138_1_p14, _74138_1_p15, _74138_1_p16,
       _74138_1_p17, _74138_1_p18, _74138_1_p19, _74138_2_p9, _74138_2_p10, _74138_2_p11, _74138_2_p12,
       _74138_2_p13, _74138_2_p14, _74138_2_p15, _74139_1_p9, _74139_1_p10, _74139_1_p11, _74154_1_p8,
       _74154_1_p9, _74154_1_p10, _74154_1_p11, _74154_1_p12, _74154_1_p13, _74154_1_p14, _74154_1_p15,
       _74154_1_p16, _74154_1_p17, _74154_1_p18, _74154_1_p19, _74154_2_p4, _74154_2_p9, _74154_2_p10,
       _74154_2_p11, _74175_1_p1, _74175_1_p2, _74175_1_p3, _74175_2_p7, _74175_2_p8, _74189_1_p13,
       _74189_1_p14, _74189_1_p15, _74189_1_p16, _74191_1_p7, _74191_2_p4, _74191_4_p11, _74191_4_p12,
       _74191_4_p13, _74191_4_p14, _74191_4_p15, _74191_5_p11, _74191_5_p12, _74191_5_p13, _74191_5_p14,
       _74191_5_p15, _74191_6_p11, _74191_6_p12, _74191_6_p13, _74191_6_p14, _74373_1_p13, _74373_1_p14,
       _74373_1_p15, _74373_1_p16, _74373_2_p13, _74373_2_p14, _74373_2_p15, _74373_2_p16, _74373_4_p13,
       _74373_4_p14, _74373_4_p15, _74373_4_p16, _74373_7_p13, _74373_7_p14, _74373_7_p15, _74373_8_p12,
       _74373_8_p13, _74373_8_p14, _74373_8_p15, _74373_9_p13, _74373_9_p14, _74373_9_p15, _74373_9_p16,
       _74373_10_p14, _74373_10_p15, _74373_10_p16, _74373_10_p17, _74373_11_p12, _74373_11_p13,
       _74373_11_p14, _74373_11_p15, _74373_12_p13, _74373_12_p14, _74373_12_p15, _74373_12_p16,
       _74373_13_p14, _74373_13_p15, _74373_13_p16, _74373_13_p17, _74373_14_p13, _74373_14_p14,
       _74373_14_p15, _74373_14_p16, _744017_1_p4, _744017_1_p5, _744017_1_p6, alu_1_carry_flag,
       alu_1_n_flag, alu_1_notequal_flag, and_1_out, and_2_out, and_3_out, and_8_out, and_9_out, clock3_2,
       delay_1_out, delay_3_out, delay_4_out, delay_5_out, nor_1_out, nor_2_out, not_1_out, not_2_out,
       not_3_out, not_4_out, not_5_out, not_6_out, not_7_out, not_8_out, not_9_out, not_10_out, not_11_out,
       not_12_out, not_13_out, not_14_out, not_15_out, not_16_out, not_17_out, not_18_out, not_19_out,
       not_20_out, not_21_out, not_22_out, not_23_out, not_24_out, not_25_out, not_26_out, or_1_out, or_2_out;
  wire [2:0] rom_2_d_2;
  wire [3:0] _74373_15_p16, driverinvsel_1_out, rom_1_d;
  wire [9:0] _74175_1_p11;
  wire [15:0] not_43_out, rom_2_d;

  ROM #(.AddrBits(3), .Bits(4)) rom_1 (.A(rom_2_d_2), .sel(1'b1), .D(rom_1_d));
  assign driverinvsel_1_out = ~_74138_1_p18 ? rom_1_d : 4'bz;  // DriverInvSel driverinvsel_1
  and and_1 (and_1_out, driverinvsel_1_out[0], not_2_out);
  and and_2 (and_2_out, driverinvsel_1_out[2], not_2_out);
  and and_3 (and_3_out, driverinvsel_1_out[1], not_2_out);
  not not_1 (not_1_out, _744017_1_p6);
  // _74191 _74191_1: pin names not known; wires that end beside it: 1'b0, 1'b0, 1'b0, 1'b0, 1'b1, 1'b0, _74191_1_p7, 1'b0, 1'b0, clk, _74175_1_p11[0], _74175_1_p11[1], _74175_1_p11[2]
  // _74191 _74191_2: pin names not known; wires that end beside it: and_1_out, and_3_out, and_2_out, _74191_2_p4, 1'b1, 1'b0, not_1_out, 1'b0, 1'b0, 1'b0, _74175_1_p11[3], _74175_1_p11[4], _74175_1_p11[5], _74175_1_p11[6]
  and and_4 (_74191_2_p4, driverinvsel_1_out[3], not_2_out);
  // _744017 _744017_1: pin names not known; wires that end beside it: 1'b1, 1'b0, 1'b0, _744017_1_p4, _744017_1_p5, _744017_1_p6, _744017_1_p5
  not not_2 (not_2_out, or_1_out);
  or or_1 (or_1_out, _74175_1_p1, _74175_1_p2, _74175_1_p3);
  nand nand_1 (_74191_1_p7, _74175_1_p11[2], _74175_1_p11[1], _74175_1_p11[0]);
  // _74175 _74175_1: pin names not known; wires that end beside it: _74175_1_p1, _74175_1_p2, _74175_1_p3, 1'b0, or_1_out, 1'b1, 1'b1, 1'b0, _74175_1_p11[7], _74175_1_p11[8], _74175_1_p11[9]
  // _74191 _74191_3: pin names not known; wires that end beside it: 1'b0, 1'b0, 1'b0, 1'b0, 1'b1, 1'b0, _74191_1_p7, 1'b0, 1'b0, clk, _744017_1_p4
  ROM #(.AddrBits(10), .Bits(16)) rom_2 (.A(_74175_1_p11), .sel(1'b1), .D({rom_2_d[15], rom_2_d_2, rom_2_d[11:0]}));
  Delay delay_1 (.in(rom_2_d[15]), .out(delay_1_out));
  Delay delay_2 (.in(_744017_1_p4), .out(clock3_2));
  // _74154 _74154_1: pin names not known; wires that end beside it: 1'b1, 1'b0, 1'b0, 1'b0, rom_2_d[0], rom_2_d[1], rom_2_d[2], _74154_1_p8, _74154_1_p9, _74154_1_p10, _74154_1_p11, _74154_1_p12, _74154_1_p13, _74154_1_p14, _74154_1_p15, _74154_1_p16, _74154_1_p17, _74154_1_p18, _74154_1_p19
  // _74138 _74138_1: pin names not known; wires that end beside it: rom_2_d[3], 1'b1, 1'b0, 1'b1, 1'b0, 1'b0, rom_2_d[4], rom_2_d[5], rom_2_d[6], _74138_1_p10, _74138_1_p11, _74138_1_p12, _74138_1_p13, _74138_1_p14, _74138_1_p15, _74138_1_p16, _74138_1_p17, _74138_1_p18, _74138_1_p19
  // _74138 _74138_2: pin names not known; wires that end beside it: 1'b1, 1'b0, 1'b1, 1'b0, 1'b0, rom_2_d[7], rom_2_d[8], rom_2_d[9], _74138_2_p9, _74138_2_p10, _74138_2_p11, _74138_2_p12, _74138_2_p13, _74138_2_p14, _74138_2_p15
  // _74139 _74139_1: pin names not known; wires that end beside it: rom_2_d[10], rom_2_d[11], 1'b0, 1'b1, 1'b1, 1'b1, 1'b1, 1'b0, _74139_1_p9, _74139_1_p10, _74139_1_p11
  not not_3 (not_3_out, _74154_1_p8);
  not not_4 (not_4_out, _74154_1_p11);
  not not_5 (not_5_out, _74154_1_p12);
  not not_6 (not_6_out, _74154_1_p13);
  not not_7 (not_7_out, _74154_1_p14);
  not not_8 (not_8_out, _74154_1_p15);
  not not_9 (not_9_out, _74154_1_p16);
  not not_10 (not_10_out, _74154_1_p17);
  not not_11 (not_11_out, _74154_1_p18);
  not not_12 (not_12_out, _74154_1_p19);
  not not_13 (not_13_out, _74138_1_p10);
  not not_14 (not_14_out, _74138_1_p11);
  not not_15 (not_15_out, _74138_1_p12);
  not not_16 (not_16_out, _74138_1_p19);
  not not_17 (not_17_out, _74138_2_p9);
  not not_18 (not_18_out, _74138_2_p10);
  not not_19 (not_19_out, _74138_2_p12);
  not not_20 (not_20_out, _74138_2_p13);
  not not_21 (not_21_out, _74138_2_p14);
  not not_22 (not_22_out, _74138_2_p15);
  Delay delay_3 (.in(_74139_1_p9), .out(delay_3_out));
  Delay delay_4 (.in(_74139_1_p10), .out(delay_4_out));
  Delay delay_5 (.in(_74139_1_p11), .out(delay_5_out));
  // _74373 _74373_1: pin names not known; wires that end beside it: 1'b0, not_12_out, driverinvsel_1_out[0], driverinvsel_1_out[1], driverinvsel_1_out[2], driverinvsel_1_out[3], 1'b0, 1'b0, 1'b0, 1'b0, 1'b1, 1'b0, _74373_1_p13, _74373_1_p14, _74373_1_p15, _74373_1_p16
  // _74373 _74373_2: pin names not known; wires that end beside it: 1'b0, not_13_out, driverinvsel_1_out[0], driverinvsel_1_out[1], driverinvsel_1_out[2], driverinvsel_1_out[3], 1'b0, 1'b0, 1'b0, 1'b0, 1'b1, 1'b0, _74373_2_p13, _74373_2_p14, _74373_2_p15, _74373_2_p16
  // _74175 _74175_2: pin names not known; wires that end beside it: driverinvsel_1_out[0], driverinvsel_1_out[1], not_15_out, 1'b1, 1'b1, 1'b0, _74175_2_p7, _74175_2_p8
  // _74373 _74373_3: pin names not known; wires that end beside it: 1'b1, 1'b0, _74138_1_p14, driverinvsel_1_out[0], driverinvsel_1_out[1], driverinvsel_1_out[2], driverinvsel_1_out[3], 1'b0, 1'b0, 1'b0, 1'b0, not_4_out, driverinvsel_1_out[0], driverinvsel_1_out[1], driverinvsel_1_out[2], driverinvsel_1_out[3]
  or or_2 (or_2_out, not_17_out, not_18_out, not_19_out, not_20_out, not_21_out);
  ALU alu_1 (
    .IN1(_74373_1_p13), .IN2(_74373_1_p14), .IN3(_74373_1_p15), .IN4(_74373_1_p16), .IN5(_74373_2_p13),
    .IN6(_74373_2_p14), .IN7(_74373_2_p15), .IN8(_74373_2_p16), .ADD(not_17_out), .CMP(not_19_out),
    .SUB(not_18_out), .CPL(not_20_out), .CMP_BIT(not_21_out), .CMP_SEL_1(_74175_2_p7),
    .CMP_SEL_2(_74175_2_p8), .CARRY_FLAG(alu_1_carry_flag), .Q0_out(driverinvsel_1_out[0]),
    .Q1_out(driverinvsel_1_out[1]), .Q2_out(driverinvsel_1_out[2]), .Q3_out(driverinvsel_1_out[3]),
    .NOTEqual_FLAG(alu_1_notequal_flag), .N_FLAG(alu_1_n_flag));
  // _74373 _74373_4: pin names not known; wires that end beside it: 1'b1, 1'b0, 1'b0, driverinvsel_1_out[0], driverinvsel_1_out[1], driverinvsel_1_out[2], driverinvsel_1_out[3], 1'b0, 1'b0, 1'b0, 1'b0, not_3_out, _74373_4_p13, _74373_4_p14, _74373_4_p15, _74373_4_p16
  // _74373 _74373_5: pin names not known; wires that end beside it: 1'b1, 1'b0, _74138_1_p16, alu_1_carry_flag, alu_1_n_flag, 1'b0, 1'b0, 1'b0, 1'b0, 1'b0, 1'b0, or_2_out, driverinvsel_1_out[0], driverinvsel_1_out[1], driverinvsel_1_out[2], driverinvsel_1_out[3]
  // _74189 _74189_1: pin names not known; wires that end beside it: _74373_4_p13, _74373_4_p14, _74373_4_p15, _74373_4_p16, driverinvsel_1_out[0], driverinvsel_1_out[1], driverinvsel_1_out[2], driverinvsel_1_out[3], _74154_1_p9, 1'b0, 1'b1, 1'b0, _74189_1_p13, _74189_1_p14, _74189_1_p15, _74189_1_p16
  not not_23 (not_23_out, _74189_1_p13);
  not not_24 (not_24_out, _74189_1_p14);
  not not_25 (not_25_out, _74189_1_p15);
  not not_26 (not_26_out, _74189_1_p16);
  assign driverinvsel_1_out[0] = ~_74138_1_p13 ? not_23_out : 1'bz;  // DriverInvSel driverinvsel_2
  assign driverinvsel_1_out[1] = ~_74138_1_p13 ? not_24_out : 1'bz;  // DriverInvSel driverinvsel_3
  assign driverinvsel_1_out[2] = ~_74138_1_p13 ? not_25_out : 1'bz;  // DriverInvSel driverinvsel_4
  assign driverinvsel_1_out[3] = ~_74138_1_p13 ? not_26_out : 1'bz;  // DriverInvSel driverinvsel_5
  // _74373 _74373_6: pin names not known; wires that end beside it: 1'b1, 1'b0, _74138_1_p15, driverinvsel_1_out[0], driverinvsel_1_out[1], driverinvsel_1_out[2], driverinvsel_1_out[3], 1'b0, 1'b0, 1'b0, 1'b0, not_5_out, driverinvsel_1_out[0], driverinvsel_1_out[1], driverinvsel_1_out[2], driverinvsel_1_out[3]
  // _74373 _74373_7: pin names not known; wires that end beside it: 1'b1, 1'b0, 1'b0, driverinvsel_1_out[0], driverinvsel_1_out[1], driverinvsel_1_out[2], 1'b0, 1'b0, 1'b0, 1'b0, 1'b0, not_14_out, _74373_7_p13, _74373_7_p14, _74373_7_p15
  Stack_FOR_MIT stack_for_mit_1 (
    .D0(driverinvsel_1_out[0]), .D1(driverinvsel_1_out[1]), .D2(driverinvsel_1_out[2]),
    .D3(driverinvsel_1_out[3]), .Clock(not_22_out), .nPUSH_POP_A(not_16_out), .Q0(driverinvsel_1_out[0]),
    .Q1(driverinvsel_1_out[1]), .Q2(driverinvsel_1_out[2]), .Q3(driverinvsel_1_out[3]));
  and and_5 (_74175_1_p1, _74373_7_p13, in_2);
  and and_6 (_74175_1_p2, _74373_7_p14, in_3);
  and and_7 (_74175_1_p3, _74373_7_p15, in_4);
  // _74373 _74373_8: pin names not known; wires that end beside it: 1'b1, 1'b0, 1'b0, driverinvsel_1_out[0], driverinvsel_1_out[1], driverinvsel_1_out[2], driverinvsel_1_out[3], 1'b0, 1'b0, 1'b0, 1'b0, _74373_8_p12, _74373_8_p13, _74373_8_p14, _74373_8_p15
  // _74373 _74373_9: pin names not known; wires that end beside it: not_6_out, 1'b1, 1'b0, 1'b0, driverinvsel_1_out[0], driverinvsel_1_out[1], driverinvsel_1_out[2], driverinvsel_1_out[3], 1'b0, 1'b0, 1'b0, 1'b0, _74373_9_p13, _74373_9_p14, _74373_9_p15, _74373_9_p16
  // _74373 _74373_10: pin names not known; wires that end beside it: not_7_out, 1'b1, 1'b0, 1'b0, driverinvsel_1_out[0], driverinvsel_1_out[1], driverinvsel_1_out[2], driverinvsel_1_out[3], 1'b0, 1'b0, 1'b0, 1'b0, not_8_out, _74373_10_p14, _74373_10_p15, _74373_10_p16, _74373_10_p17
  and and_8 (and_8_out, _74138_2_p11, ~alu_1_notequal_flag);  // And
  // _74191 _74191_4: pin names not known; wires that end beside it: _74373_8_p12, _74373_8_p13, _74373_8_p14, _74373_8_p15, 1'b1, 1'b0, and_8_out, 1'b0, 1'b0, clock3_2, _74191_4_p11, _74191_4_p12, _74191_4_p13, _74191_4_p14, _74191_4_p15
  // _74191 _74191_5: pin names not known; wires that end beside it: _74373_9_p13, _74373_9_p14, _74373_9_p15, _74373_9_p16, 1'b1, 1'b0, and_8_out, 1'b0, _74191_4_p11, clock3_2, _74191_5_p11, _74191_5_p12, _74191_5_p13, _74191_5_p14, _74191_5_p15
  // _74191 _74191_6: pin names not known; wires that end beside it: _74373_10_p14, _74373_10_p15, _74373_10_p16, _74373_10_p17, 1'b1, 1'b0, and_8_out, 1'b0, _74191_5_p11, clock3_2, _74191_6_p11, _74191_6_p12, _74191_6_p13, _74191_6_p14
  // _74373 _74373_11: pin names not known; wires that end beside it: 1'b1, 1'b0, 1'b0, driverinvsel_1_out[0], driverinvsel_1_out[1], driverinvsel_1_out[2], driverinvsel_1_out[3], driverinvsel_1_out[0], driverinvsel_1_out[1], driverinvsel_1_out[2], driverinvsel_1_out[3], _74373_11_p12, _74373_11_p13, _74373_11_p14, _74373_11_p15
  // _74373 _74373_12: pin names not known; wires that end beside it: not_9_out, 1'b1, 1'b0, 1'b0, driverinvsel_1_out[0], driverinvsel_1_out[1], driverinvsel_1_out[2], driverinvsel_1_out[3], 1'b0, 1'b0, 1'b0, 1'b0, _74373_12_p13, _74373_12_p14, _74373_12_p15, _74373_12_p16
  // _74373 _74373_13: pin names not known; wires that end beside it: not_10_out, 1'b1, 1'b0, 1'b0, driverinvsel_1_out[0], driverinvsel_1_out[1], driverinvsel_1_out[2], driverinvsel_1_out[3], 1'b0, 1'b0, 1'b0, 1'b0, not_11_out, _74373_13_p14, _74373_13_p15, _74373_13_p16, _74373_13_p17
  // _74244 _74244_1: pin names not known; wires that end beside it: delay_4_out, delay_3_out, driverinvsel_1_out[0], 1'b0, driverinvsel_1_out[0], _74191_4_p12, driverinvsel_1_out[1], _74191_5_p12, driverinvsel_1_out[1], _74191_4_p13, driverinvsel_1_out[2], _74191_5_p13, driverinvsel_1_out[2], _74191_4_p14
  // _74244 _74244_2: pin names not known; wires that end beside it: driverinvsel_1_out[3], _74191_5_p14, driverinvsel_1_out[3], _74191_4_p15, _74191_5_p15, 1'b1, delay_5_out, 1'b1, driverinvsel_1_out[0], 1'b0, _74191_6_p11, driverinvsel_1_out[1], 1'b0, _74191_6_p12, driverinvsel_1_out[2], 1'b0, _74191_6_p13, driverinvsel_1_out[3], 1'b0, _74191_6_p14, 1'b0
  and and_9 (and_9_out, _74154_1_p10, _74138_1_p17);
  // _74154 _74154_2: pin names not known; wires that end beside it: 1'b1, 1'b0, and_9_out, _74154_2_p4, _74373_13_p14, _74373_13_p15, _74373_13_p16, _74373_13_p17, _74154_2_p9, _74154_2_p10, _74154_2_p11
  not not_27 (_74154_2_p4, delay_1_out);
  // _28c64 _28c64_1: pin names not known; wires that end beside it: 1'b1, 1'b0, _74191_4_p12, _74191_4_p13, _74191_4_p14, _74191_4_p15, _74191_5_p12, _74191_5_p13, _74191_5_p14, _74191_5_p15, _74191_6_p11, _74191_6_p12, _74191_6_p13, _74191_6_p14, 1'b0, 1'b0, 1'b1, delay_1_out, driverinvsel_1_out[0], driverinvsel_1_out[1], driverinvsel_1_out[2], driverinvsel_1_out[3]
  // A623308A a623308a_1: pin names not known; wires that end beside it: _74373_11_p12, _74373_11_p13, _74373_11_p14, _74373_11_p15, _74373_12_p13, _74373_12_p14, _74373_12_p15, _74373_12_p16, 1'b0, 1'b0, 1'b0, 1'b0, 1'b0, _74154_2_p9, _74138_1_p17, _74154_1_p10, 1'b1, 1'b0, driverinvsel_1_out[0], driverinvsel_1_out[1], driverinvsel_1_out[2], driverinvsel_1_out[3]
  nor nor_1 (nor_1_out, _74154_2_p10, _74154_1_p10);
  // _74373 _74373_14: pin names not known; wires that end beside it: 1'b1, 1'b0, 1'b0, driverinvsel_1_out[0], driverinvsel_1_out[1], driverinvsel_1_out[2], driverinvsel_1_out[3], 1'b0, 1'b0, 1'b0, 1'b0, nor_1_out, _74373_14_p13, _74373_14_p14, _74373_14_p15, _74373_14_p16
  // _74154 _74154_3: pin names not known; wires that end beside it: 1'b1, 1'b0, 1'b0, 1'b0, _74373_14_p13, _74373_14_p14, _74373_14_p15, _74373_14_p16
  nor nor_2 (nor_2_out, _74154_2_p11, _74154_1_p10);
  // Not not_28 has open pins: in=open, out=not_43_out[0]
  // Not not_29 has open pins: in=open, out=not_43_out[1]
  // Not not_30 has open pins: in=open, out=not_43_out[2]
  // Not not_31 has open pins: in=open, out=not_43_out[3]
  // Not not_32 has open pins: in=open, out=not_43_out[4]
  // Not not_33 has open pins: in=open, out=not_43_out[5]
  // Not not_34 has open pins: in=open, out=not_43_out[6]
  // Not not_35 has open pins: in=open, out=not_43_out[7]
  // Not not_36 has open pins: in=open, out=not_43_out[8]
  // Not not_37 has open pins: in=open, out=not_43_out[9]
  // Not not_38 has open pins: in=open, out=not_43_out[10]
  // Not not_39 has open pins: in=open, out=not_43_out[11]
  // Not not_40 has open pins: in=open, out=not_43_out[12]
  // Not not_41 has open pins: in=open, out=not_43_out[13]
  // Not not_42 has open pins: in=open, out=not_43_out[14]
  // Not not_43 has open pins: in=open, out=not_43_out[15]
  // _74373 _74373_15: pin names not known; wires that end beside it: 1'b1, 1'b0, 1'b0, driverinvsel_1_out[0], driverinvsel_1_out[1], driverinvsel_1_out[2], driverinvsel_1_out[3], 1'b0, 1'b0, 1'b0, 1'b0, nor_2_out, _74373_15_p16[0], _74373_15_p16[1], _74373_15_p16[2], _74373_15_p16[3]
  LedMatrix #(.colAddrBits(4), .rowDataBits(16)) ledmatrix_1 (.rows(not_43_out), .column(_74373_15_p16));

  // Other names for the same wires on the sheet: clock2 = clk

  // Notes on the sheet:
  //   clk: Hz: 200
  //   CPU
  //   contents of rom_1 (hex, n*v repeats v):
  //   4,c0,6*0,8
  //   contents of rom_2 (hex, n*v repeats v):
  //   9*0,1,0,2,5*0,1,8015,1,8032,4*0,1,19,1,1a,1,1b,8023,0,1,19,1,1a
  //   ,1,1b,8054,0,1,8014,6*0,1,8022,6*0,e,7*0,6,8780,7,8b80,8,8f80
  //   ,180,0,6,0,7,0,8,0,200,0,1,801c,1,801d,1,8082,0,0,1,801c,1,801d
  //   ,1,8102,0,0,6,0,7,0,8,0,300,0,1,801c,1,80c2,4*0,83f6,83f7,83f8
  //   ,180,4*0,1,801c,1,801d,1,801f
  //   INT
  //   ADDRESS_other
  //   ADDRESS_ROM
  //   DATA BUS
endmodule
